// Logisim project adder.circ as structural Verilog: 4 circuits, main circuit main
module main (
  input  [3:0] Input_A,
  input  [3:0] Input_B
);

  wire divisibility_1_divisibility_by_2, divisibility_1_divisibility_by_3, divisibility_1_divisibility_by_4,
       n7448_1_p8, n7448_1_p9, n7448_1_p10, n7448_1_p11, n7448_1_p12, n7448_1_p13, n7448_1_p14,
       ones_digit_1_a, ones_digit_1_b, ones_digit_1_c, ones_digit_1_d, ones_digit_1_e, ones_digit_1_f,
       ones_digit_1_g;
  wire [3:0] adder_1_out, tens_digit_1_output;
  wire [4:4] adder_1_cout;

  Adder #(.width(4)) adder_1 (.a(Input_A), .b(Input_B), .out(adder_1_out), .cin(1'b0), .cout(adder_1_cout[4]));
  Tens_digit tens_digit_1 (.Input({adder_1_cout[4], adder_1_out}), .Output(tens_digit_1_output));
  Divisibility divisibility_1 (
    .Divisibility_by_2(divisibility_1_divisibility_by_2),
    .Divisibility_by_3(divisibility_1_divisibility_by_3), .Input({adder_1_cout[4], adder_1_out}),
    .Divisibility_by_4(divisibility_1_divisibility_by_4));
  Ones_digit ones_digit_1 (
    .Input({adder_1_cout[4], adder_1_out}), .a(ones_digit_1_a), .b(ones_digit_1_b), .c(ones_digit_1_c),
    .d(ones_digit_1_d), .e(ones_digit_1_e), .f(ones_digit_1_f), .g(ones_digit_1_g));
  // _7448 7448_1: pin names not known; wires that end beside it: tens_digit_1_output[1], tens_digit_1_output[2], 1'b1, 1'b1, 1'b1, tens_digit_1_output[3], tens_digit_1_output[0], n7448_1_p8, n7448_1_p9, n7448_1_p10, n7448_1_p11, n7448_1_p12, n7448_1_p13, n7448_1_p14
  _7_Segment_Display u_7_segment_display_1 (
    .g(n7448_1_p9), .f(n7448_1_p8), .a(n7448_1_p10), .b(n7448_1_p11), .e(n7448_1_p14), .d(n7448_1_p13),
    .c(n7448_1_p12));  // open: dp
  _7_Segment_Display u_7_segment_display_2 (
    .g(ones_digit_1_g), .f(ones_digit_1_f), .a(ones_digit_1_a), .b(ones_digit_1_b), .e(ones_digit_1_e),
    .d(ones_digit_1_d), .c(ones_digit_1_c));  // open: dp
  LED Divisible_by_2 (.in(divisibility_1_divisibility_by_2));
  LED Divisible_by_3 (.in(divisibility_1_divisibility_by_3));
  LED Divisible_by_4 (.in(divisibility_1_divisibility_by_4));

  // Notes on the sheet:
  //   MSB
  //   LSB
  //   LSB
  //   MSB
  //   Tens
  //   Ones
  //   SUM
endmodule

module Tens_digit (
  input  [4:0] Input,
  output [3:0] Output
);

  wire B0_out, B1_out, B2_out, C1_out, C2_out, C3_out, comparator_1_eq, comparator_1_gt, comparator_2_eq,
       comparator_2_gt, comparator_3_eq, comparator_3_gt;

  Comparator #(.width(5), .mode("unsigned")) comparator_1 (
    .a(Input), .b(5'b01010), .gt(comparator_1_gt), .eq(comparator_1_eq));  // open: lt
  Comparator #(.width(5), .mode("unsigned")) comparator_2 (
    .a(Input), .b(5'b10100), .gt(comparator_2_gt), .eq(comparator_2_eq));  // open: lt
  Comparator #(.width(5), .mode("unsigned")) comparator_3 (
    .a(Input), .b(5'b11110), .gt(comparator_3_gt), .eq(comparator_3_eq));  // open: lt
  or C1 (C1_out, comparator_1_gt, comparator_1_eq);
  or C2 (C2_out, comparator_2_gt, comparator_2_eq);
  or C3 (C3_out, comparator_3_gt, comparator_3_eq);
  and B1 (B1_out, C1_out, ~C2_out);  // AND_Gate
  and B2 (B2_out, C2_out, ~C3_out);  // AND_Gate
  assign Output = B1_out ? 4'b0001 : 4'bz;  // Controlled_Buffer controlled_buffer_1
  assign Output = B2_out ? 4'b0010 : 4'bz;  // Controlled_Buffer controlled_buffer_2
  not B0 (B0_out, C1_out);
  assign Output = C3_out ? 4'b0011 : 4'bz;  // Controlled_Buffer controlled_buffer_3
  assign Output = B0_out ? 4'b0000 : 4'bz;  // Controlled_Buffer controlled_buffer_4

  // Notes on the sheet:
  //   MSB
  //   LSB
  //   MSB
  //   LSB
endmodule

module Ones_digit (
  input  [4:0] Input,
  output g,
  output d,
  output a,
  output e,
  output b,
  output f,
  output c
);

  wire and_1_out, and_2_out, and_3_out, and_4_out, and_5_out, and_6_out, and_7_out, and_8_out, and_9_out,
       nand_1_out, nand_2_out, nand_3_out, or_1_out, or_2_out, or_3_out, or_4_out, or_5_out, or_6_out,
       or_7_out, or_8_out, or_9_out, or_10_out, or_11_out, or_12_out, or_13_out, or_14_out, or_15_out,
       or_16_out, or_17_out, or_18_out, or_19_out, or_20_out, or_21_out, or_22_out, or_23_out, or_24_out,
       or_25_out, or_26_out, or_27_out, or_28_out, or_29_out, or_30_out, or_31_out;

  or or_1 (or_1_out, Input[4], Input[3], ~Input[2], Input[1], Input[0]);  // OR_Gate
  or or_2 (or_2_out, ~Input[4], ~Input[3], Input[2], Input[1], Input[0]);  // OR_Gate
  or or_3 (or_3_out, Input[4], Input[3], Input[2], Input[1], ~Input[0]);  // OR_Gate
  or or_4 (or_4_out, ~Input[4], Input[3], ~Input[2], Input[1], ~Input[0]);  // OR_Gate
  or or_5 (or_5_out, Input[4], ~Input[3], Input[2], ~Input[1], ~Input[0]);  // OR_Gate
  nand nand_1 (nand_1_out, Input[4], Input[3], Input[2], Input[1], Input[0]);
  or or_6 (or_6_out, Input[4], ~Input[3], ~Input[2], ~Input[1], Input[0]);  // OR_Gate
  or or_7 (or_7_out, ~Input[4], Input[3], Input[2], Input[1], Input[0]);  // OR_Gate
  or or_8 (or_8_out, Input[4], Input[3], ~Input[2], Input[1], ~Input[0]);  // OR_Gate
  or or_9 (or_9_out, ~Input[4], ~Input[3], Input[2], Input[1], ~Input[0]);  // OR_Gate
  or or_10 (or_10_out, Input[4], ~Input[3], ~Input[2], ~Input[1], ~Input[0]);  // OR_Gate
  or or_11 (or_11_out, Input[4], Input[3], ~Input[2], ~Input[1], Input[0]);  // OR_Gate
  or or_12 (or_12_out, ~Input[4], ~Input[3], Input[2], ~Input[1], Input[0]);  // OR_Gate
  or or_13 (or_13_out, Input[4], ~Input[3], ~Input[2], Input[1], Input[0]);  // OR_Gate
  or or_14 (or_14_out, Input[4], Input[3], Input[2], ~Input[1], Input[0]);  // OR_Gate
  or or_15 (or_15_out, ~Input[4], Input[3], ~Input[2], ~Input[1], Input[0]);  // OR_Gate
  and and_1 (and_1_out, or_1_out, or_2_out, or_3_out, or_4_out, or_5_out);
  and and_2 (and_2_out, nand_1_out, or_6_out);
  and and_3 (and_3_out, or_7_out, or_8_out, or_9_out);
  and and_4 (and_4_out, or_10_out, or_11_out, or_12_out);
  and u_c (c, or_13_out, or_14_out, or_15_out);
  and u_a (a, and_1_out, and_2_out);
  and u_b (b, and_3_out, and_4_out);
  or or_16 (or_16_out, Input[3], Input[2], Input[1], ~Input[0]);  // OR_Gate
  or or_17 (or_17_out, ~Input[4], Input[3], Input[1], ~Input[0]);  // OR_Gate
  or or_18 (or_18_out, Input[4], Input[3], ~Input[2], ~Input[1], ~Input[0]);  // OR_Gate
  nand nand_2 (nand_2_out, Input[4], Input[3], Input[1], Input[0]);
  or or_19 (or_19_out, ~Input[3], Input[2], ~Input[1], ~Input[0]);  // OR_Gate
  or or_20 (or_20_out, Input[4], ~Input[3], ~Input[2], ~Input[1], Input[0]);  // OR_Gate
  or or_21 (or_21_out, Input[4], Input[3], ~Input[2], Input[1]);  // OR_Gate
  or or_22 (or_22_out, Input[4], ~Input[3], ~Input[2], ~Input[1]);  // OR_Gate
  or or_23 (or_23_out, ~Input[4], ~Input[3], Input[2], Input[1]);  // OR_Gate
  or or_24 (or_24_out, Input[4], Input[3], Input[2], ~Input[1]);  // OR_Gate
  or or_25 (or_25_out, Input[4], Input[3], ~Input[1], ~Input[0]);  // OR_Gate
  or or_26 (or_26_out, Input[4], ~Input[3], ~Input[2], Input[1]);  // OR_Gate
  or or_27 (or_27_out, ~Input[4], Input[3], ~Input[2], ~Input[0]);  // OR_Gate
  or or_28 (or_28_out, ~Input[4], Input[3], ~Input[2], ~Input[1]);  // OR_Gate
  and and_5 (and_5_out, or_16_out, or_19_out, nand_2_out);
  and and_6 (and_6_out, or_24_out, or_25_out, or_26_out, or_27_out, or_28_out);
  and and_7 (and_7_out, or_1_out, or_2_out, or_16_out, or_17_out);
  and and_8 (and_8_out, or_18_out, nand_2_out, or_19_out, or_20_out);
  and u_e (e, or_21_out, or_22_out, or_23_out, ~Input[0]);  // AND_Gate
  and u_f (f, and_5_out, and_6_out);
  and u_d (d, and_7_out, and_8_out);
  or or_29 (or_29_out, Input[4], Input[3], Input[2], Input[1]);
  or or_30 (or_30_out, Input[4], ~Input[3], Input[2], ~Input[1]);  // OR_Gate
  and and_9 (and_9_out, or_18_out, or_17_out, or_19_out);
  or or_31 (or_31_out, ~Input[4], Input[3], ~Input[2], Input[1]);  // OR_Gate
  nand nand_3 (nand_3_out, Input[4], Input[3], Input[2], Input[1]);
  and u_g (g, or_29_out, or_30_out, and_9_out, or_31_out, nand_3_out);

  // Notes on the sheet:
  //   MSB
  //   ABCDE
  //   LSB
endmodule

module Divisibility (
  input  [4:0] Input,
  output Divisibility_by_2,
  output Divisibility_by_3,
  output Divisibility_by_4
);

  wire and_1_out, and_2_out, and_3_out, and_4_out, and_5_out, and_6_out, and_7_out, and_8_out, and_9_out,
       and_10_out, nor_1_out, or_1_out, or_2_out, or_3_out;

  nor nor_1 (nor_1_out, Input[4], Input[3], Input[2], Input[1], Input[0]);
  and and_1 (and_1_out, ~Input[4], Input[3], Input[2], ~Input[1], ~Input[0]);  // AND_Gate
  and and_2 (and_2_out, Input[4], Input[3], ~Input[2], ~Input[1], ~Input[0]);  // AND_Gate
  and and_3 (and_3_out, ~Input[4], Input[3], ~Input[2], ~Input[1], Input[0]);  // AND_Gate
  and and_4 (and_4_out, Input[4], ~Input[3], Input[2], ~Input[1], Input[0]);  // AND_Gate
  and and_5 (and_5_out, ~Input[4], ~Input[3], ~Input[2], Input[1], Input[0]);  // AND_Gate
  and and_6 (and_6_out, ~Input[4], Input[3], Input[2], Input[1], Input[0]);  // AND_Gate
  and and_7 (and_7_out, Input[4], Input[3], ~Input[2], Input[1], Input[0]);  // AND_Gate
  and and_8 (and_8_out, ~Input[4], ~Input[3], Input[2], Input[1], ~Input[0]);  // AND_Gate
  and and_9 (and_9_out, Input[4], ~Input[3], ~Input[2], Input[1], ~Input[0]);  // AND_Gate
  and and_10 (and_10_out, Input[4], Input[3], Input[2], Input[1], ~Input[0]);  // AND_Gate
  nor nor_2 (Divisibility_by_4, Input[1], Input[0]);
  or or_1 (or_1_out, nor_1_out, and_1_out, and_2_out, and_3_out);
  or or_2 (or_2_out, and_4_out, and_5_out, and_6_out, and_7_out);
  or or_3 (or_3_out, and_8_out, and_9_out, and_10_out);
  not not_1 (Divisibility_by_2, Input[0]);
  or or_4 (Divisibility_by_3, or_1_out, or_2_out, or_3_out);

  // Notes on the sheet:
  //   MSB
  //   ABCDE
  //   LSB
endmodule
