// Logisim project counter.circ as structural Verilog: 5 circuits, main circuit main
module main (
);

  wire bcd_to_7_segment_1_a_2, bcd_to_7_segment_1_b_2, bcd_to_7_segment_1_c_2, bcd_to_7_segment_1_d_2,
       bcd_to_7_segment_1_e, bcd_to_7_segment_1_f, bcd_to_7_segment_1_g, Button_out, Clock_out,
       display_mode_0_1_a, display_mode_0_1_b, display_mode_0_1_c, display_mode_0_1_d, display_mode_0_1_e,
       display_mode_0_1_f, display_mode_1_1_a_2, display_mode_1_1_b, display_mode_1_1_c, display_mode_1_1_d,
       display_mode_1_1_stop, or_1_out, switch_2_a, switch_2_b, switch_2_c, switch_2_d, switch_2_e,
       switch_2_f, switch_2_g, Switch_p2;

  Clock Clock (.out(Clock_out));
  Button Button (.out(Button_out));
  // Switch_part Switch: pin names not known; wires that end beside it: 1'b1, Switch_p2
  Pull_Resistor pull_resistor_1 (.node(Switch_p2));
  Display_Mode_0 display_mode_0_1 (
    .CLK(Clock_out), .X(Button_out), .a(display_mode_0_1_a), .b(display_mode_0_1_b), .c(display_mode_0_1_c),
    .d(display_mode_0_1_d), .e(display_mode_0_1_e), .f(display_mode_0_1_f));
  Display_Mode_1 display_mode_1_1 (
    .CLK(Clock_out), .a(display_mode_0_1_a), .D(display_mode_1_1_d), .C(display_mode_1_1_c),
    .B(display_mode_1_1_b), .A_2(display_mode_1_1_a_2), .STOP(display_mode_1_1_stop));
  or or_1 (or_1_out, Switch_p2, display_mode_1_1_stop);
  BCD_to_7_segment bcd_to_7_segment_1 (
    .D(display_mode_1_1_d), .C(display_mode_1_1_c), .B(display_mode_1_1_b), .A(display_mode_1_1_a_2),
    .e(bcd_to_7_segment_1_e), .f(bcd_to_7_segment_1_f), .g(bcd_to_7_segment_1_g),
    .d_2(bcd_to_7_segment_1_d_2), .c_2(bcd_to_7_segment_1_c_2), .b_2(bcd_to_7_segment_1_b_2),
    .a_2(bcd_to_7_segment_1_a_2));
  Switch switch_2 (
    .a0(display_mode_0_1_a), .b0(display_mode_0_1_b), .c0(display_mode_0_1_c), .d0(display_mode_0_1_d),
    .e0(display_mode_0_1_e), .f0(display_mode_0_1_f), .a1(bcd_to_7_segment_1_a_2),
    .b1(bcd_to_7_segment_1_b_2), .c1(bcd_to_7_segment_1_c_2), .d1(bcd_to_7_segment_1_d_2),
    .e1(bcd_to_7_segment_1_e), .f1(bcd_to_7_segment_1_f), .g1(bcd_to_7_segment_1_g), .a(switch_2_a),
    .b(switch_2_b), .c(switch_2_c), .d(switch_2_d), .e(switch_2_e), .f(switch_2_f), .g(switch_2_g),
    .Switch(or_1_out));
  _7_Segment_Display u_7_segment_display_1 (
    .g(switch_2_g), .f(switch_2_f), .a(switch_2_a), .b(switch_2_b), .e(switch_2_e), .d(switch_2_d),
    .c(switch_2_c));  // open: dp
endmodule

// DM0
module Display_Mode_0 (
  input  CLK,
  input  X,
  output a,
  output b,
  output c,
  output d,
  output e,
  output f
);

  wire and_1_out, and_2_out, and_3_out, and_4_out, and_5_out, and_6_out, and_7_out, and_8_out, and_9_out,
       and_11_out, and_12_out, and_13_out, D0_qn, D1_q, D1_qn, D2_q, D2_qn, not_1_out, or_1_out, or_2_out,
       or_3_out;

  not not_1 (not_1_out, X);
  and and_1 (and_1_out, c, D1_qn);
  and and_2 (and_2_out, not_1_out, c);
  and and_3 (and_3_out, X, D1_q, D2_q);
  and and_4 (and_4_out, X, D1_qn, D2_q);
  and and_5 (and_5_out, not_1_out, D1_q);
  and and_6 (and_6_out, D0_qn, D1_q, D2_qn);
  and and_7 (and_7_out, not_1_out, D2_q);
  and and_8 (and_8_out, X, D1_qn, D2_qn);
  and and_9 (and_9_out, X, D0_qn, D2_qn);
  or or_1 (or_1_out, and_1_out, and_2_out, and_3_out);
  or or_2 (or_2_out, and_4_out, and_5_out, and_6_out);
  or or_3 (or_3_out, and_7_out, and_8_out, and_9_out);
  D_Flip_Flop #(.Pre_Clr_Positions("LEGACY"), .enable("true"), .NewFFLayout("false")) D0 (
    .clk(CLK), .D(or_1_out), .Q(c), .Qn(D0_qn));  // open: preset, en, reset
  D_Flip_Flop #(.Pre_Clr_Positions("LEGACY"), .enable("true"), .NewFFLayout("false")) D1 (
    .clk(CLK), .D(or_2_out), .Q(D1_q), .Qn(D1_qn));  // open: preset, en, reset
  D_Flip_Flop #(.Pre_Clr_Positions("LEGACY"), .enable("true"), .NewFFLayout("false")) D2 (
    .clk(CLK), .D(or_3_out), .Q(D2_q), .Qn(D2_qn));  // open: preset, en, reset
  and and_10 (a, c, D1_q);
  and and_11 (and_11_out, c, D2_q);
  or or_4 (b, and_11_out, and_12_out);
  and and_12 (and_12_out, c, D1_q);
  or or_5 (d, c, and_13_out);
  and and_13 (and_13_out, D1_q, D2_q);
  or or_6 (e, c, D1_q);
  or or_7 (f, c, D1_q, D2_q);
endmodule

// DM1
module Display_Mode_1 (
  input  CLK,
  input  a,
  output D,
  output C,
  output B,
  output A_2,
  output STOP
);

  wire and_1_out, counter_qn, d_ff_1_qn, d_ff_2_qn, d_ff_3_qn, delay_qn;

  and and_1 (and_1_out, a, ~STOP);  // AND_Gate
  D_Flip_Flop #(.Pre_Clr_Positions("LEGACY"), .enable("true"), .NewFFLayout("false")) delay (
    .clk(CLK), .D(and_1_out), .Qn(delay_qn));  // open: Q, preset, en, reset
  D_Flip_Flop #(.Pre_Clr_Positions("LEGACY"), .enable("true"), .NewFFLayout("false")) counter (
    .clk(delay_qn), .D(counter_qn), .Q(D), .Qn(counter_qn));  // open: preset, en, reset
  D_Flip_Flop #(.Pre_Clr_Positions("LEGACY"), .enable("true"), .NewFFLayout("false")) d_ff_1 (
    .clk(counter_qn), .D(d_ff_1_qn), .Q(C), .Qn(d_ff_1_qn));  // open: preset, en, reset
  D_Flip_Flop #(.Pre_Clr_Positions("LEGACY"), .enable("true"), .NewFFLayout("false")) d_ff_2 (
    .clk(d_ff_1_qn), .D(d_ff_2_qn), .Q(B), .Qn(d_ff_2_qn));  // open: preset, en, reset
  D_Flip_Flop #(.Pre_Clr_Positions("LEGACY"), .enable("true"), .NewFFLayout("false")) d_ff_3 (
    .clk(d_ff_2_qn), .D(d_ff_3_qn), .Q(A_2), .Qn(d_ff_3_qn));  // open: preset, en, reset
  and and_2 (STOP, C, A_2);
endmodule

// Switcher
module Switch (
  input  a0,
  input  b0,
  input  c0,
  input  d0,
  input  e0,
  input  f0,
  input  a1,
  input  b1,
  input  c1,
  input  d1,
  input  e1,
  input  f1,
  input  g1,
  input  Switch,
  output a,
  output b,
  output c,
  output d,
  output e,
  output f,
  output g
);

  Multiplexer #(.enable("false")) multiplexer_1 (.in0(a0), .in1(a1), .out(a), .sel(Switch));
  and and_1 (g, g1, Switch);
  Multiplexer #(.enable("false")) multiplexer_2 (.in0(b0), .in1(b1), .out(b), .sel(Switch));
  Multiplexer #(.enable("false")) multiplexer_3 (.in0(c0), .in1(c1), .out(c), .sel(Switch));
  Multiplexer #(.enable("false")) multiplexer_4 (.in0(d0), .in1(d1), .out(d), .sel(Switch));
  Multiplexer #(.enable("false")) multiplexer_5 (.in0(e0), .in1(e1), .out(e), .sel(Switch));
  Multiplexer #(.enable("false")) multiplexer_6 (.in0(f0), .in1(f1), .out(f), .sel(Switch));
endmodule

// Decoder
module BCD_to_7_segment (
  input  D,
  input  C,
  input  B,
  input  A,
  output a_2,
  output b_2,
  output c_2,
  output d_2,
  output e,
  output f,
  output g
);

  wire or_1_out, or_2_out, or_3_out, or_4_out, or_5_out, or_6_out, or_7_out, or_8_out, or_9_out, or_10_out,
       or_11_out;

  or or_1 (or_1_out, ~B, C, D);  // OR_Gate
  or or_2 (or_2_out, A, B, C, ~D);  // OR_Gate
  or or_3 (or_3_out, ~B, C, ~D);  // OR_Gate
  or or_4 (or_4_out, ~B, ~C, D);  // OR_Gate
  or or_5 (or_5_out, ~B, ~C, ~D);  // OR_Gate
  or or_6 (or_6_out, ~A, ~C);  // OR_Gate
  or or_7 (or_7_out, ~B, C);  // OR_Gate
  or or_8 (or_8_out, A, B, ~D);  // OR_Gate
  or or_9 (or_9_out, ~C, ~D);  // OR_Gate
  or or_10 (or_10_out, A, B, ~C);  // OR_Gate
  or or_11 (or_11_out, A, B, C);
  and and_1 (a_2, or_1_out, or_2_out);
  and and_2 (b_2, or_3_out, or_4_out);
  or or_12 (c_2, A, B, ~C, D);  // OR_Gate
  and and_3 (d_2, a_2, or_5_out, or_6_out);
  and and_4 (e, or_7_out, ~D);  // AND_Gate
  and and_5 (f, or_8_out, or_9_out, or_10_out);
  and and_6 (g, or_11_out, or_5_out);

  // Notes on the sheet:
  //   Note that this only counts to 10
endmodule
